# Fritzing sketch CNC_USB_Interface_V20_Trial6 (saved by Fritzing 0.9.2b)
circuit board: 11.4cm x 16.1cm
breadboards: 1

parts:
  UM245R1 = FTDI UM245R [part_number=UM245R package="DIP (Dual Inline) [THT]"]
  74166 = 74LS166 [package="DIP (Dual Inline) [THT]"]
  74164 = 74LS164 [package="DIP (Dual Inline) [THT]"]
  J1 = male pin header, 8 pins [form="♂ (male)"]
  74574 = 74LS574 [part_number=DM74LS574 package="DIP (Dual Inline) [THT]"]
  74164_2 = 74LS164 [package="DIP (Dual Inline) [THT]"]
  J2 = male pin header, 8 pins [form="♂ (male)"]
  74166_2 = 74LS166 [package="DIP (Dual Inline) [THT]"]
  J3 = male pin header, 8 pins [form="♂ (male)"]
  J4 = male pin header, 8 pins [form="♂ (male)"]
  74574_2 = 74LS574 [part_number=DM74LS574 package="DIP (Dual Inline) [THT]"]
  74164_3 = 74LS164 [package="DIP (Dual Inline) [THT]"]
  J5 = male pin header, 8 pins [form="♂ (male)"]
  LED1 = LED - 5mm [color="Red (633nm)" package="5 mm [THT]"]
  R1 = Resistor [tolerance=±5% resistance=220 package=THT]
  IC1 = IC, SIP package, 10 pins [chip_label=res]
  IC2 = IC, SIP package, 10 pins [chip_label=res]
  J7 = male pin header, 2 pins [form="♂ (male)"]
  J8 = male pin header, 2 pins [form="♂ (male)"]
  J6 = Screw terminal - 2 pins [package=THT]
  74574_3 = 74LS574 [part_number=DM74LS574 package="DIP (Dual Inline) [THT]"]
  C1 = Tantalum Capacitor [capacitance=1μF package="100 mil [THT, tantalum]"]
  C2 = Tantalum Capacitor [capacitance=1μF package="100 mil [THT, tantalum]"]
  C3 = Tantalum Capacitor [capacitance=1μF package="100 mil [THT, tantalum]"]
  J9 = male pin header, 2 pins [form="♂ (male)"]
  J10 = male pin header, 2 pins [form="♂ (male)"]

nets:
  N1: UM245R1.DB0, 74166_2.QH
  N2: UM245R1.DB4, 74166.S/L#, 74166_2.S/L#
  N3: UM245R1.DB2, 74166.QH
  N4: UM245R1.DB1, 74164_2.A, 74164_2.B
  N5: UM245R1.DB7, 74166.CLK, 74164.CP, 74164_2.CP, 74166_2.CLK, 74164_3.CP
  GND: UM245R1.GND, 74166.SerIn, 74166.CKI, 74166.GND, 74164.GND, 74574.OE#, 74574.GND, 74164_2.GND, 74166_2.SerIn, 74166_2.CKI, 74166_2.GND, 74574_2.OE#, 74574_2.GND, 74164_3.GND, IC1.pin1, IC2.pin1, J7.pin1, J8.pin1, J6.pin2, 74574_3.OE#, 74574_3.GND, C1.-, C2.-, C3.-, J9.pin1, J10.pin1
  N6: UM245R1.DB5, 74164_3.A, 74164_3.B
  N7: UM245R1.DB6, 74164.A, 74164.B
  N8: UM245R1.DB3, 74574.CP, 74574_2.CP, 74574_3.CP
  N9: UM245R1.RXF#, LED1.cathode
  N10: 74166.A, J3.pin8, IC2.pin10
  N11: 74166.B, J3.pin7, IC2.pin9
  N12: 74166.C, J3.pin6, IC2.pin8
  N13: 74166.D, J3.pin5, IC2.pin7
  VCC: 74166.CLR#, 74166.VCC, 74164.MR#, 74164.VCC, 74574.VCC, 74164_2.MR#, 74164_2.VCC, 74166_2.CLR#, 74166_2.VCC, 74574_2.VCC, 74164_3.MR#, 74164_3.VCC, R1.Pin_0, J7.pin2, J8.pin2, J6.pin1, 74574_3.VCC, C1.+, C2.+, C3.+, J9.pin2, J10.pin2
  N14: 74166.E, J3.pin4, IC2.pin6
  N15: 74166.F, J3.pin3, IC2.pin5
  N16: 74166.G, J3.pin2, IC2.pin4
  N17: 74166.H, J3.pin1, IC2.pin3
  N18: 74164.Q0, 74574_3.D7
  N19: 74164.Q1, 74574_3.D6
  N20: 74164.Q2, 74574_3.D5
  N21: 74164.Q3, 74574_3.D4
  N22: 74164.Q4, 74574_3.D3
  N23: 74164.Q5, 74574_3.D2
  N24: 74164.Q6, 74574_3.D1
  N25: 74164.Q7, 74574_3.D0
  N26: J1.pin1, 74574_3.O0
  N27: J1.pin2, 74574_3.O1
  N28: J1.pin3, 74574_3.O2
  N29: J1.pin4, 74574_3.O3
  N30: J1.pin5, 74574_3.O4
  N31: J1.pin6, 74574_3.O5
  N32: J1.pin7, 74574_3.O6
  N33: J1.pin8, 74574_3.O7
  N34: 74574.D0, 74164_2.Q7
  N35: 74574.D1, 74164_2.Q6
  N36: 74574.D2, 74164_2.Q5
  N37: 74574.D3, 74164_2.Q4
  N38: 74574.D4, 74164_2.Q3
  N39: 74574.D5, 74164_2.Q2
  N40: 74574.D6, 74164_2.Q1
  N41: 74574.D7, 74164_2.Q0
  N42: 74574.O7, J2.pin8
  N43: 74574.O6, J2.pin7
  N44: 74574.O5, J2.pin6
  N45: 74574.O4, J2.pin5
  N46: 74574.O3, J2.pin4
  N47: 74574.O2, J2.pin3
  N48: 74574.O1, J2.pin2
  N49: 74574.O0, J2.pin1
  N50: 74166_2.A, J4.pin8, IC1.pin10
  N51: 74166_2.B, J4.pin7, IC1.pin9
  N52: 74166_2.C, J4.pin6, IC1.pin8
  N53: 74166_2.D, J4.pin5, IC1.pin7
  N54: 74166_2.E, J4.pin4, IC1.pin6
  N55: 74166_2.F, J4.pin3, IC1.pin5
  N56: 74166_2.G, J4.pin2, IC1.pin4
  N57: 74166_2.H, J4.pin1, IC1.pin3
  N58: 74574_2.D0, 74164_3.Q7
  N59: 74574_2.D1, 74164_3.Q6
  N60: 74574_2.D2, 74164_3.Q5
  N61: 74574_2.D3, 74164_3.Q4
  N62: 74574_2.D4, 74164_3.Q3
  N63: 74574_2.D5, 74164_3.Q2
  N64: 74574_2.D6, 74164_3.Q1
  N65: 74574_2.D7, 74164_3.Q0
  N66: 74574_2.O7, J5.pin8
  N67: 74574_2.O6, J5.pin7
  N68: 74574_2.O5, J5.pin6
  N69: 74574_2.O4, J5.pin5
  N70: 74574_2.O3, J5.pin4
  N71: 74574_2.O2, J5.pin3
  N72: 74574_2.O1, J5.pin2
  N73: 74574_2.O0, J5.pin1
  N74: LED1.anode, R1.Pin_1

notes:
  Parallel to Serial USB Interface V2.0
  Emmanuel Charette - Nov. 2015
  Output Byte 2
  Output Byte 1
  Output Byte 0
  Input Byte 1
  Input Byte 0

custom parts:
  FTDI UM245R: FTDI UM245R USB to parrallel interface
  74LS166: 8 Bit Shift Register
  74LS164: Serial-In Parallel-Out Shift Register
  74LS574: Octal D-Type Flip-Flop with 3-State Outputs
